// Logisim project sequence-counter.circ as structural Verilog: 6 circuits, main circuit main
module main (
  input  X,
  input  RESET
);

  wire CLK_out, sequence_detector_1_s1, sequence_detector_1_s2, sequence_detector_1_s3;
  wire [3:0] sequence_detector_1_actual;
  wire [6:0] CEN1, CEN2, CEN3, DEC1, DEC2, DEC3, UNI1, UNI2, UNI3;
  wire [7:0] event_counter_1_c1, event_counter_1_c2, event_counter_1_c3;

  Clock CLK (.out(CLK_out));
  _7_Segment_Display u_7_segment_display_1 (
    .g(CEN1[0]), .f(CEN1[1]), .a(CEN1[6]), .b(CEN1[5]), .e(CEN1[2]), .d(CEN1[3]), .c(CEN1[4]));  // open: dp
  _7_Segment_Display u_7_segment_display_2 (
    .g(CEN2[0]), .f(CEN2[1]), .a(CEN2[6]), .b(CEN2[5]), .e(CEN2[2]), .d(CEN2[3]), .c(CEN2[4]));  // open: dp
  _7_Segment_Display u_7_segment_display_3 (
    .g(CEN3[0]), .f(CEN3[1]), .a(CEN3[6]), .b(CEN3[5]), .e(CEN3[2]), .d(CEN3[3]), .c(CEN3[4]));  // open: dp
  // Probe on sequence_detector_1_actual
  Sequence_Detector sequence_detector_1 (
    .ACTUAL(sequence_detector_1_actual), .S3(sequence_detector_1_s3), .S1(sequence_detector_1_s1),
    .S2(sequence_detector_1_s2), .X(X), .CLK(CLK_out), .RESET(RESET));
  LED S1 (.in(sequence_detector_1_s1));
  LED S2 (.in(sequence_detector_1_s2));
  LED S3 (.in(sequence_detector_1_s3));
  _7_Segment_Display u_7_segment_display_4 (
    .g(DEC1[0]), .f(DEC1[1]), .a(DEC1[6]), .b(DEC1[5]), .e(DEC1[2]), .d(DEC1[3]), .c(DEC1[4]));  // open: dp
  _7_Segment_Display u_7_segment_display_5 (
    .g(DEC2[0]), .f(DEC2[1]), .a(DEC2[6]), .b(DEC2[5]), .e(DEC2[2]), .d(DEC2[3]), .c(DEC2[4]));  // open: dp
  _7_Segment_Display u_7_segment_display_6 (
    .g(DEC3[0]), .f(DEC3[1]), .a(DEC3[6]), .b(DEC3[5]), .e(DEC3[2]), .d(DEC3[3]), .c(DEC3[4]));  // open: dp
  // Probe on event_counter_1_c3
  // Probe on event_counter_1_c2
  // Probe on event_counter_1_c1
  Event_Counter event_counter_1 (
    .C1(event_counter_1_c1), .C2(event_counter_1_c2), .C3(event_counter_1_c3), .CLK(CLK_out), .RESET(RESET),
    .S1(sequence_detector_1_s1), .S2(sequence_detector_1_s2), .S3(sequence_detector_1_s3));
  _7_Segment_Display u_7_segment_display_7 (
    .g(UNI1[0]), .f(UNI1[1]), .a(UNI1[6]), .b(UNI1[5]), .e(UNI1[2]), .d(UNI1[3]), .c(UNI1[4]));  // open: dp
  _7_Segment_Display u_7_segment_display_8 (
    .g(UNI2[0]), .f(UNI2[1]), .a(UNI2[6]), .b(UNI2[5]), .e(UNI2[2]), .d(UNI2[3]), .c(UNI2[4]));  // open: dp
  _7_Segment_Display u_7_segment_display_9 (
    .g(UNI3[0]), .f(UNI3[1]), .a(UNI3[6]), .b(UNI3[5]), .e(UNI3[2]), .d(UNI3[3]), .c(UNI3[4]));  // open: dp
  Visualization visualization_1 (
    .DEC1(DEC1), .UNI1(UNI1), .CEN2(CEN2), .DEC2(DEC2), .UNI2(UNI2), .CEN3(CEN3), .DEC3(DEC3), .UNI3(UNI3),
    .CEN1(CEN1), .C1(event_counter_1_c1), .C2(event_counter_1_c2), .C3(event_counter_1_c3));

  // Notes on the sheet:
  //   SECUENCIA #1: 1110
  //   SECUENCIA #2: 11000
  //   SECUENCIA #3: 100101
endmodule

module Sequence_Detector (
  input  CLK,
  input  RESET,
  input  X,
  output S1,
  output S2,
  output [3:0] ACTUAL,
  output S3
);

  wire and_4_out, and_5_out, and_6_out, and_7_out, and_8_out, and_9_out, and_10_out, and_11_out, and_12_out,
       and_13_out, and_14_out, and_15_out, and_16_out, and_17_out, and_18_out, and_19_out, and_20_out,
       and_21_out, and_22_out, and_23_out, and_24_out, and_25_out, J0, J1, J2, J3, K0, K1, K2, K3, not_1_out,
       not_2_out, not_3_out, not_4_out, not_5_out;

  not not_1 (not_1_out, ACTUAL[3]);
  not not_2 (not_2_out, ACTUAL[2]);
  not not_3 (not_3_out, ACTUAL[1]);
  not not_4 (not_4_out, ACTUAL[0]);
  not not_5 (not_5_out, X);
  and and_1 (S1, ACTUAL[3], not_3_out, ACTUAL[0]);
  and and_2 (S2, ACTUAL[3], ACTUAL[1], ACTUAL[0]);
  and and_3 (S3, ACTUAL[3], ACTUAL[2]);
  and and_4 (and_4_out, ACTUAL[2], ACTUAL[0], not_5_out);
  and and_5 (and_5_out, ACTUAL[2], ACTUAL[1], not_5_out);
  and and_6 (and_6_out, not_3_out, X);
  and and_7 (and_7_out, ACTUAL[1], not_5_out);
  and and_8 (and_8_out, ACTUAL[1], ACTUAL[0]);
  and and_9 (and_9_out, ACTUAL[1], not_4_out, not_5_out);
  and and_10 (and_10_out, not_1_out, ACTUAL[1], ACTUAL[0]);
  and and_11 (and_11_out, ACTUAL[3], not_4_out, X);
  or or_1 (K2, not_5_out, ACTUAL[0], ACTUAL[3]);
  and and_12 (and_12_out, not_1_out, not_2_out, ACTUAL[0]);
  and and_13 (and_13_out, ACTUAL[2], not_4_out, X);
  and and_14 (and_14_out, ACTUAL[3], not_4_out);
  and and_15 (and_15_out, not_2_out, not_4_out);
  and and_16 (and_16_out, not_2_out, not_5_out);
  and and_17 (and_17_out, not_4_out, not_5_out);
  and and_18 (and_18_out, not_1_out, not_2_out, X);
  and and_19 (and_19_out, not_3_out, X);
  and and_20 (and_20_out, ACTUAL[2], ACTUAL[1], not_5_out);
  and and_21 (and_21_out, ACTUAL[3], not_2_out, not_3_out);
  and and_22 (and_22_out, not_3_out, not_5_out);
  and and_23 (and_23_out, not_1_out, not_2_out, ACTUAL[1], X);
  and and_24 (and_24_out, ACTUAL[2], not_5_out);
  and and_25 (and_25_out, ACTUAL[3], not_5_out);
  or or_2 (J3, and_4_out, and_5_out);
  or or_3 (K3, and_6_out, and_7_out, and_8_out, ACTUAL[2]);
  or or_4 (J2, and_9_out, and_10_out, and_11_out);
  or or_5 (J1, and_12_out, and_13_out, and_14_out);
  or or_6 (K1, and_15_out, and_16_out, and_17_out, ACTUAL[3]);
  or or_7 (J0, and_18_out, and_19_out, and_20_out, and_21_out);
  or or_8 (K0, and_22_out, and_23_out, and_24_out, and_25_out);
  LED Seq1 (.in(S1));
  LED Seq2 (.in(S2));
  LED Seq3 (.in(S3));
  // Probe on ACTUAL
  J_K_Flip_Flop j_k_ff_1 (.J(J3), .K(K3), .clk(CLK), .Q(ACTUAL[3]), .reset(RESET));  // open: Qn, preset
  J_K_Flip_Flop j_k_ff_2 (.J(J2), .K(K2), .clk(CLK), .Q(ACTUAL[2]), .reset(RESET));  // open: Qn, preset
  J_K_Flip_Flop j_k_ff_3 (.J(J1), .K(K1), .clk(CLK), .Q(ACTUAL[1]), .reset(RESET));  // open: Qn, preset
  J_K_Flip_Flop j_k_ff_4 (.J(J0), .K(K0), .clk(CLK), .Q(ACTUAL[0]), .reset(RESET));  // open: Qn, preset

  // Other names for the same wires on the sheet: Q0 = ACTUAL[0]; Q1 = ACTUAL[1]; Q2 = ACTUAL[2]; Q3 = ACTUAL[3]
endmodule

module Visualization (
  input  [7:0] C1,
  input  [7:0] C2,
  input  [7:0] C3,
  output [6:0] CEN1,
  output [6:0] DEC1,
  output [6:0] UNI1,
  output [6:0] CEN2,
  output [6:0] DEC2,
  output [6:0] UNI2,
  output [6:0] CEN3,
  output [6:0] DEC3,
  output [6:0] UNI3
);

  wire [3:0] bcd_1_centena, bcd_1_decena, bcd_1_unidad, bcd_2_centena, bcd_2_decena, bcd_2_unidad,
       bcd_3_centena, bcd_3_decena, bcd_3_unidad;

  BCD bcd_1 (.UNIDAD(bcd_1_unidad), .CENTENA(bcd_1_centena), .DECENA(bcd_1_decena), .CONTADOR(C1));
  BCD bcd_2 (.UNIDAD(bcd_2_unidad), .CENTENA(bcd_2_centena), .DECENA(bcd_2_decena), .CONTADOR(C2));
  BCD bcd_3 (.UNIDAD(bcd_3_unidad), .CENTENA(bcd_3_centena), .DECENA(bcd_3_decena), .CONTADOR(C3));
  LED_Config led_config_1 (.NUMERO(bcd_1_centena), .LED(CEN1));
  LED_Config led_config_2 (.NUMERO(bcd_1_decena), .LED(DEC1));
  LED_Config led_config_3 (.NUMERO(bcd_1_unidad), .LED(UNI1));
  LED_Config led_config_4 (.NUMERO(bcd_2_centena), .LED(CEN2));
  LED_Config led_config_5 (.NUMERO(bcd_2_decena), .LED(DEC2));
  LED_Config led_config_6 (.NUMERO(bcd_2_unidad), .LED(UNI2));
  LED_Config led_config_7 (.NUMERO(bcd_3_centena), .LED(CEN3));
  LED_Config led_config_8 (.NUMERO(bcd_3_decena), .LED(DEC3));
  LED_Config led_config_9 (.NUMERO(bcd_3_unidad), .LED(UNI3));
endmodule

module LED_Config (
  input  [3:0] NUMERO,
  output [6:0] LED
);

  wire and_1_out, and_2_out, and_3_out, and_4_out, and_5_out, and_6_out, and_7_out, and_8_out, and_9_out,
       and_10_out, and_11_out, and_12_out, and_13_out, and_14_out, and_15_out, and_16_out, not_1_out,
       not_2_out, not_3_out;

  not not_1 (not_1_out, NUMERO[2]);
  not not_2 (not_2_out, NUMERO[1]);
  not not_3 (not_3_out, NUMERO[0]);
  and and_1 (and_1_out, not_1_out, not_3_out);
  and and_2 (and_2_out, NUMERO[2], NUMERO[0]);
  and and_3 (and_3_out, not_2_out, not_3_out);
  and and_4 (and_4_out, NUMERO[1], NUMERO[0]);
  or or_1 (LED[4], not_2_out, NUMERO[0], NUMERO[2]);
  and and_5 (and_5_out, not_1_out, not_3_out);
  and and_6 (and_6_out, not_1_out, NUMERO[1]);
  and and_7 (and_7_out, NUMERO[1], not_3_out);
  and and_8 (and_8_out, NUMERO[2], not_2_out, NUMERO[0]);
  and and_9 (and_9_out, not_1_out, not_3_out);
  and and_10 (and_10_out, NUMERO[1], not_3_out);
  and and_11 (and_11_out, not_2_out, not_3_out);
  and and_12 (and_12_out, NUMERO[2], not_2_out);
  and and_13 (and_13_out, NUMERO[2], not_3_out);
  and and_14 (and_14_out, not_1_out, NUMERO[1]);
  and and_15 (and_15_out, NUMERO[2], not_2_out);
  and and_16 (and_16_out, NUMERO[2], not_3_out);
  or or_2 (LED[6], and_1_out, NUMERO[1], and_2_out, NUMERO[3]);
  or or_3 (LED[5], not_1_out, and_3_out, and_4_out);
  or or_4 (LED[3], and_5_out, and_6_out, and_7_out, and_8_out, NUMERO[3]);
  or or_5 (LED[2], and_9_out, and_10_out);
  or or_6 (LED[1], and_11_out, and_12_out, and_13_out, NUMERO[3]);
  or or_7 (LED[0], and_14_out, and_15_out, and_16_out, NUMERO[3]);
endmodule

module BCD (
  input  [7:0] CONTADOR,
  output [3:0] CENTENA,
  output [3:0] DECENA,
  output [3:0] UNIDAD
);

  wire [7:0] divider_1_out;
  wire [7:4] divider_1_rem, divider_2_out, divider_2_rem;

  Divider divider_1 (.a(CONTADOR), .b(8'ha), .out(divider_1_out), .rem({divider_1_rem, UNIDAD}));  // open: upper
  Divider divider_2 (
    .a(divider_1_out), .b(8'ha), .out({divider_2_out, CENTENA}), .rem({divider_2_rem, DECENA}));  // open: upper
endmodule

module Event_Counter (
  input  S1,
  input  CLK,
  input  RESET,
  input  S2,
  input  S3,
  output [7:0] C1,
  output [7:0] C2,
  output [7:0] C3
);

  wire and_1_out, and_2_out, and_3_out, and_4_out, and_5_out, and_6_out, and_7_out, and_8_out, and_9_out,
       and_10_out, and_11_out, and_12_out, and_13_out, and_14_out, and_15_out, and_16_out, and_17_out,
       and_18_out, and_19_out, and_20_out, and_21_out;

  J_K_Flip_Flop j_k_ff_1 (.J(S1), .K(S1), .clk(CLK), .Q(C1[0]), .reset(RESET));  // open: Qn, preset
  J_K_Flip_Flop j_k_ff_2 (.J(S2), .K(S2), .clk(CLK), .Q(C2[0]), .reset(RESET));  // open: Qn, preset
  J_K_Flip_Flop j_k_ff_3 (.J(S3), .K(S3), .clk(CLK), .Q(C3[0]), .reset(RESET));  // open: Qn, preset
  J_K_Flip_Flop j_k_ff_4 (.J(and_1_out), .K(and_1_out), .clk(CLK), .Q(C1[1]), .reset(RESET));  // open: Qn, preset
  and and_1 (and_1_out, C1[0], S1);
  J_K_Flip_Flop j_k_ff_5 (.J(and_2_out), .K(and_2_out), .clk(CLK), .Q(C2[1]), .reset(RESET));  // open: Qn, preset
  and and_2 (and_2_out, C2[0], S2);
  J_K_Flip_Flop j_k_ff_6 (.J(and_3_out), .K(and_3_out), .clk(CLK), .Q(C3[1]), .reset(RESET));  // open: Qn, preset
  and and_3 (and_3_out, C3[0], S3);
  J_K_Flip_Flop j_k_ff_7 (.J(and_4_out), .K(and_4_out), .clk(CLK), .Q(C1[2]), .reset(RESET));  // open: Qn, preset
  and and_4 (and_4_out, C1[1], and_1_out);
  J_K_Flip_Flop j_k_ff_8 (.J(and_5_out), .K(and_5_out), .clk(CLK), .Q(C2[2]), .reset(RESET));  // open: Qn, preset
  and and_5 (and_5_out, C2[1], and_2_out);
  J_K_Flip_Flop j_k_ff_9 (.J(and_6_out), .K(and_6_out), .clk(CLK), .Q(C3[2]), .reset(RESET));  // open: Qn, preset
  and and_6 (and_6_out, C3[1], and_3_out);
  and and_7 (and_7_out, C1[2], and_4_out);
  and and_8 (and_8_out, C2[2], and_5_out);
  and and_9 (and_9_out, C3[2], and_6_out);
  J_K_Flip_Flop j_k_ff_10 (.J(and_7_out), .K(and_7_out), .clk(CLK), .Q(C1[3]), .reset(RESET));  // open: Qn, preset
  J_K_Flip_Flop j_k_ff_11 (.J(and_8_out), .K(and_8_out), .clk(CLK), .Q(C2[3]), .reset(RESET));  // open: Qn, preset
  J_K_Flip_Flop j_k_ff_12 (.J(and_9_out), .K(and_9_out), .clk(CLK), .Q(C3[3]), .reset(RESET));  // open: Qn, preset
  J_K_Flip_Flop j_k_ff_13 (.J(and_10_out), .K(and_10_out), .clk(CLK), .Q(C1[4]), .reset(RESET));  // open: Qn, preset
  and and_10 (and_10_out, C1[3], and_7_out);
  J_K_Flip_Flop j_k_ff_14 (.J(and_11_out), .K(and_11_out), .clk(CLK), .Q(C2[4]), .reset(RESET));  // open: Qn, preset
  and and_11 (and_11_out, C2[3], and_8_out);
  J_K_Flip_Flop j_k_ff_15 (.J(and_12_out), .K(and_12_out), .clk(CLK), .Q(C3[4]), .reset(RESET));  // open: Qn, preset
  and and_12 (and_12_out, C3[3], and_9_out);
  J_K_Flip_Flop j_k_ff_16 (.J(and_13_out), .K(and_13_out), .clk(CLK), .Q(C1[5]), .reset(RESET));  // open: Qn, preset
  and and_13 (and_13_out, C1[4], and_10_out);
  J_K_Flip_Flop j_k_ff_17 (.J(and_14_out), .K(and_14_out), .clk(CLK), .Q(C2[5]), .reset(RESET));  // open: Qn, preset
  and and_14 (and_14_out, C2[4], and_11_out);
  J_K_Flip_Flop j_k_ff_18 (.J(and_15_out), .K(and_15_out), .clk(CLK), .Q(C3[5]), .reset(RESET));  // open: Qn, preset
  and and_15 (and_15_out, C3[4], and_12_out);
  and and_16 (and_16_out, C1[5], and_13_out);
  and and_17 (and_17_out, C2[5], and_14_out);
  and and_18 (and_18_out, C3[5], and_15_out);
  J_K_Flip_Flop j_k_ff_19 (.J(and_16_out), .K(and_16_out), .clk(CLK), .Q(C1[6]), .reset(RESET));  // open: Qn, preset
  J_K_Flip_Flop j_k_ff_20 (.J(and_17_out), .K(and_17_out), .clk(CLK), .Q(C2[6]), .reset(RESET));  // open: Qn, preset
  J_K_Flip_Flop j_k_ff_21 (.J(and_18_out), .K(and_18_out), .clk(CLK), .Q(C3[6]), .reset(RESET));  // open: Qn, preset
  J_K_Flip_Flop j_k_ff_22 (.J(and_19_out), .K(and_19_out), .clk(CLK), .Q(C1[7]), .reset(RESET));  // open: Qn, preset
  and and_19 (and_19_out, C1[6], and_16_out);
  J_K_Flip_Flop j_k_ff_23 (.J(and_20_out), .K(and_20_out), .clk(CLK), .Q(C2[7]), .reset(RESET));  // open: Qn, preset
  and and_20 (and_20_out, C2[6], and_17_out);
  J_K_Flip_Flop j_k_ff_24 (.J(and_21_out), .K(and_21_out), .clk(CLK), .Q(C3[7]), .reset(RESET));  // open: Qn, preset
  and and_21 (and_21_out, C3[6], and_18_out);

  // Other names for the same wires on the sheet: Q10 = C1[0]; Q11 = C1[1]; Q12 = C1[2]; Q13 = C1[3]; Q14 = C1[4];
  //   Q15 = C1[5]; Q16 = C1[6]; Q17 = C1[7]; Q20 = C2[0]; Q21 = C2[1]; Q22 = C2[2]; Q23 = C2[3]; Q24 = C2[4];
  //   Q25 = C2[5]; Q26 = C2[6]; Q27 = C2[7]; Q30 = C3[0]; Q31 = C3[1]; Q32 = C3[2]; Q33 = C3[3]; Q34 = C3[4];
  //   Q35 = C3[5]; Q36 = C3[6]; Q37 = C3[7]
endmodule
