// Logisim project Alternative.circ as structural Verilog: 7 circuits, main circuit main
module main (
);

  wire alu_1_zero, and_1_out, and_2_out, CLK_out, control_1_alusrc, control_1_branchequal,
       control_1_branchnotequal, control_1_jump, control_1_memread, control_1_memtoreg, control_1_memwrite,
       control_1_regdst, control_1_regwrite, jr, lbu, Link, not_1_out, Reset_out;
  wire [1:0] control_1_aluop;
  wire [2:0] alu_control_1_alu_operation;
  wire [4:0] instruction_memory_1_instruction_2, instruction_memory_1_instruction_3, multiplexer_1_out,
       multiplexer_2_out;
  wire [5:0] instruction_memory_1_instruction_4;
  wire [15:0] instruction_memory_1_instruction;
  wire [27:0] bit_extender_1_out, shifter_1_out;
  wire [31:0] adder_2_out, alu_1_result, bit_extender_2_out, data_memory_1_readdata, multiplexer_3_out,
       multiplexer_4_out, multiplexer_5_out, multiplexer_6_out, multiplexer_7_out, multiplexer_8_out,
       multiplexer_9_out, PC_4, PC_q, Reg1, regfile_1_readdata2, shifter_2_out;

  Clock CLK (.out(CLK_out));
  Button Reset (.out(Reset_out));
  Register #(.width(32)) PC (.D(multiplexer_8_out), .clk(CLK_out), .Q(PC_q), .clr(Reset_out));  // open: en
  // Probe on {instruction_memory_1_instruction_4, instruction_memory_1_instruction_3, instruction_memory_1_instruction_2, instruction_memory_1_instruction}
  Adder #(.width(32)) adder_1 (.a(PC_q), .b(32'h4), .out(PC_4));  // open: cin, cout
  Instruction_memory instruction_memory_1 (
    .Instruction({instruction_memory_1_instruction_4, instruction_memory_1_instruction_3, instruction_memory_1_instruction_2, instruction_memory_1_instruction}),
    .ReadAddress(PC_q));
  Multiplexer #(.width(5)) multiplexer_1 (
    .in0(instruction_memory_1_instruction_2), .in1(instruction_memory_1_instruction[15:11]),
    .out(multiplexer_1_out), .sel(control_1_regdst));
  assign bit_extender_1_out = {{2{1'b0}}, {instruction_memory_1_instruction_3, instruction_memory_1_instruction_2, instruction_memory_1_instruction}};  // Bit_Extender bit_extender_1
  Multiplexer #(.width(5)) multiplexer_2 (
    .in0(multiplexer_1_out), .in1({5{1'b1}}), .out(multiplexer_2_out), .sel(Link));
  Shifter #(.width(28)) shifter_1 (.in(bit_extender_1_out), .\dist (5'b00010), .out(shifter_1_out));
  assign bit_extender_2_out = {{16{instruction_memory_1_instruction[15]}}, instruction_memory_1_instruction};  // Bit_Extender bit_extender_2
  Multiplexer #(.width(32)) multiplexer_3 (.in0(multiplexer_9_out), .in1(PC_4), .out(multiplexer_3_out), .sel(Link));
  Control control_1 (
    .ALUSrc(control_1_alusrc), .MemtoReg(control_1_memtoreg), .RegWrite(control_1_regwrite),
    .MemRead(control_1_memread), .MemWrite(control_1_memwrite), .BranchEqual(control_1_branchequal),
    .BranchNotEqual(control_1_branchnotequal), .ALUOp(control_1_aluop), .Jump(control_1_jump), .Link(Link),
    .lbu(lbu), .RegDst(control_1_regdst), .Opcode(instruction_memory_1_instruction_4));
  RegFile regfile_1 (
    .ReadData2(regfile_1_readdata2), .ReadData1(Reg1), .CLK(CLK_out), .Reset(Reset_out),
    .EnableWrite(control_1_regwrite), .ReadReg1(instruction_memory_1_instruction_3),
    .ReadReg2(instruction_memory_1_instruction_2), .WriteReg(multiplexer_2_out), .WriteData(multiplexer_3_out));
  Shifter #(.width(32)) shifter_2 (.in(bit_extender_2_out), .\dist (5'b00010), .out(shifter_2_out));
  Multiplexer #(.width(32)) multiplexer_4 (
    .in0(regfile_1_readdata2), .in1(bit_extender_2_out), .out(multiplexer_4_out), .sel(control_1_alusrc));
  Adder #(.width(32)) adder_2 (.a(PC_4), .b(shifter_2_out), .out(adder_2_out));  // open: cin, cout
  ALU_control alu_control_1 (
    .ALU_Operation(alu_control_1_alu_operation), .jr(jr), .ALUOp(control_1_aluop),
    .funct(instruction_memory_1_instruction[5:0]));
  Multiplexer #(.width(32)) multiplexer_5 (.in0(PC_4), .in1(adder_2_out), .out(multiplexer_5_out), .sel(and_1_out));
  and and_1 (and_1_out, control_1_branchequal, alu_1_zero);
  not not_1 (not_1_out, alu_1_zero);
  ALU alu_1 (
    .Result(alu_1_result), .Zero(alu_1_zero), .In2(multiplexer_4_out), .In1(Reg1),
    .ALU_Operation(alu_control_1_alu_operation));
  // Probe on regfile_1_readdata2
  Multiplexer #(.width(32)) multiplexer_6 (
    .in0(multiplexer_5_out), .in1(adder_2_out), .out(multiplexer_6_out), .sel(and_2_out));
  and and_2 (and_2_out, control_1_branchnotequal, not_1_out);
  Multiplexer #(.width(32)) multiplexer_7 (
    .in0(multiplexer_6_out), .in1({PC_4[31:28], shifter_1_out}), .out(multiplexer_7_out), .sel(control_1_jump));
  Data_memory data_memory_1 (
    .ReadData(data_memory_1_readdata), .Address(alu_1_result), .MemWrite(control_1_memwrite),
    .MemRead(control_1_memread), .CLK(CLK_out), .WriteData(regfile_1_readdata2), .lbu(lbu));
  Multiplexer #(.width(32)) multiplexer_8 (.in0(multiplexer_7_out), .in1(Reg1), .out(multiplexer_8_out), .sel(jr));
  Multiplexer #(.width(32)) multiplexer_9 (
    .in0(alu_1_result), .in1(data_memory_1_readdata), .out(multiplexer_9_out), .sel(control_1_memtoreg));
endmodule

module RegFile (
  input  CLK,
  input  Reset,
  input  [4:0] ReadReg1,
  input  [4:0] ReadReg2,
  input  [4:0] WriteReg,
  input  [31:0] WriteData,
  input  EnableWrite,
  output [31:0] ReadData1,
  output [31:0] ReadData2
);

  wire decoder_1_out1, decoder_1_out2, decoder_1_out3, decoder_1_out4, decoder_1_out5, decoder_1_out6,
       decoder_1_out7, decoder_1_out8, decoder_1_out9, decoder_1_out10, decoder_1_out11, decoder_1_out12,
       decoder_1_out13, decoder_1_out14, decoder_1_out15, decoder_1_out16, decoder_1_out17, decoder_1_out18,
       decoder_1_out19, decoder_1_out20, decoder_1_out21, decoder_1_out22, decoder_1_out23, decoder_1_out24,
       decoder_1_out25, decoder_1_out26, decoder_1_out27, decoder_1_out28, decoder_1_out29, decoder_1_out30,
       decoder_1_out31;
  wire [31:0] R0, R1, R2, R3, R4, R5, R6, R7, R8, R9, R10, R11, R12, R13, R14, R15, R16, R17, R18, R19, R20,
       R21, R22, R23, R24, R25, R26, R27, R28, R29, R30, R31;

  Register #(.width(32)) zero (.D({32{1'b0}}), .clk(CLK), .Q(R0), .clr(Reset));  // open: en
  Register #(.width(32)) at (.D(WriteData), .en(decoder_1_out1), .clk(CLK), .Q(R1), .clr(Reset));
  Register #(.width(32)) v0 (.D(WriteData), .en(decoder_1_out2), .clk(CLK), .Q(R2), .clr(Reset));
  Register #(.width(32)) v1 (.D(WriteData), .en(decoder_1_out3), .clk(CLK), .Q(R3), .clr(Reset));
  Register #(.width(32)) a0 (.D(WriteData), .en(decoder_1_out4), .clk(CLK), .Q(R4), .clr(Reset));
  Multiplexer #(.select(5), .width(32)) multiplexer_1 (
    .in0(R0), .in1(R1), .in2(R2), .in3(R3), .in4(R4), .in5(R5), .in6(R6), .in7(R7), .in8(R8), .in9(R9),
    .in10(R10), .in11(R11), .in12(R12), .in13(R13), .in14(R14), .in15(R15), .in16(R16), .in17(R17),
    .in18(R18), .in19(R19), .in20(R20), .in21(R21), .in22(R22), .in23(R23), .in24(R24), .in25(R25),
    .in26(R26), .in27(R27), .in28(R28), .in29(R29), .in30(R30), .in31(R31), .out(ReadData1), .sel(ReadReg1));
  Register #(.width(32)) a1 (.D(WriteData), .en(decoder_1_out5), .clk(CLK), .Q(R5), .clr(Reset));
  Register #(.width(32)) a2 (.D(WriteData), .en(decoder_1_out6), .clk(CLK), .Q(R6), .clr(Reset));
  Register #(.width(32)) a3 (.D(WriteData), .en(decoder_1_out7), .clk(CLK), .Q(R7), .clr(Reset));
  Register #(.width(32)) t0 (.D(WriteData), .en(decoder_1_out8), .clk(CLK), .Q(R8), .clr(Reset));
  Register #(.width(32)) t1 (.D(WriteData), .en(decoder_1_out9), .clk(CLK), .Q(R9), .clr(Reset));
  Register #(.width(32)) t2 (.D(WriteData), .en(decoder_1_out10), .clk(CLK), .Q(R10), .clr(Reset));
  Multiplexer #(.select(5), .width(32)) multiplexer_2 (
    .in0(R0), .in1(R1), .in2(R2), .in3(R3), .in4(R4), .in5(R5), .in6(R6), .in7(R7), .in8(R8), .in9(R9),
    .in10(R10), .in11(R11), .in12(R12), .in13(R13), .in14(R14), .in15(R15), .in16(R16), .in17(R17),
    .in18(R18), .in19(R19), .in20(R20), .in21(R21), .in22(R22), .in23(R23), .in24(R24), .in25(R25),
    .in26(R26), .in27(R27), .in28(R28), .in29(R29), .in30(R30), .in31(R31), .out(ReadData2), .sel(ReadReg2));
  Register #(.width(32)) t3 (.D(WriteData), .en(decoder_1_out11), .clk(CLK), .Q(R11), .clr(Reset));
  Register #(.width(32)) t4 (.D(WriteData), .en(decoder_1_out12), .clk(CLK), .Q(R12), .clr(Reset));
  Register #(.width(32)) t5 (.D(WriteData), .en(decoder_1_out13), .clk(CLK), .Q(R13), .clr(Reset));
  Register #(.width(32)) t6 (.D(WriteData), .en(decoder_1_out14), .clk(CLK), .Q(R14), .clr(Reset));
  Decoder #(.select(5)) decoder_1 (
    .out1(decoder_1_out1), .out2(decoder_1_out2), .out3(decoder_1_out3), .out4(decoder_1_out4),
    .out5(decoder_1_out5), .out6(decoder_1_out6), .out7(decoder_1_out7), .out8(decoder_1_out8),
    .out9(decoder_1_out9), .out10(decoder_1_out10), .out11(decoder_1_out11), .out12(decoder_1_out12),
    .out13(decoder_1_out13), .out14(decoder_1_out14), .out15(decoder_1_out15), .out16(decoder_1_out16),
    .out17(decoder_1_out17), .out18(decoder_1_out18), .out19(decoder_1_out19), .out20(decoder_1_out20),
    .out21(decoder_1_out21), .out22(decoder_1_out22), .out23(decoder_1_out23), .out24(decoder_1_out24),
    .out25(decoder_1_out25), .out26(decoder_1_out26), .out27(decoder_1_out27), .out28(decoder_1_out28),
    .out29(decoder_1_out29), .out30(decoder_1_out30), .out31(decoder_1_out31), .sel(WriteReg),
    .en(EnableWrite));  // open: out0
  Register #(.width(32)) t7 (.D(WriteData), .en(decoder_1_out15), .clk(CLK), .Q(R15), .clr(Reset));
  Register #(.width(32)) s0 (.D(WriteData), .en(decoder_1_out16), .clk(CLK), .Q(R16), .clr(Reset));
  Register #(.width(32)) s1 (.D(WriteData), .en(decoder_1_out17), .clk(CLK), .Q(R17), .clr(Reset));
  Register #(.width(32)) s2 (.D(WriteData), .en(decoder_1_out18), .clk(CLK), .Q(R18), .clr(Reset));
  Register #(.width(32)) s3 (.D(WriteData), .en(decoder_1_out19), .clk(CLK), .Q(R19), .clr(Reset));
  Register #(.width(32)) s4 (.D(WriteData), .en(decoder_1_out20), .clk(CLK), .Q(R20), .clr(Reset));
  Register #(.width(32)) s5 (.D(WriteData), .en(decoder_1_out21), .clk(CLK), .Q(R21), .clr(Reset));
  Register #(.width(32)) s6 (.D(WriteData), .en(decoder_1_out22), .clk(CLK), .Q(R22), .clr(Reset));
  Register #(.width(32)) s7 (.D(WriteData), .en(decoder_1_out23), .clk(CLK), .Q(R23), .clr(Reset));
  Register #(.width(32)) t8 (.D(WriteData), .en(decoder_1_out24), .clk(CLK), .Q(R24), .clr(Reset));
  Register #(.width(32)) t9 (.D(WriteData), .en(decoder_1_out25), .clk(CLK), .Q(R25), .clr(Reset));
  Register #(.width(32)) k0 (.D(WriteData), .en(decoder_1_out26), .clk(CLK), .Q(R26), .clr(Reset));
  Register #(.width(32)) k1 (.D(WriteData), .en(decoder_1_out27), .clk(CLK), .Q(R27), .clr(Reset));
  Register #(.width(32)) gp (.D(WriteData), .en(decoder_1_out28), .clk(CLK), .Q(R28), .clr(Reset));
  Register #(.width(32)) sp (.D(WriteData), .en(decoder_1_out29), .clk(CLK), .Q(R29), .clr(Reset));
  Register #(.width(32)) fp (.D(WriteData), .en(decoder_1_out30), .clk(CLK), .Q(R30), .clr(Reset));
  Register #(.width(32)) ra (.D(WriteData), .en(decoder_1_out31), .clk(CLK), .Q(R31), .clr(Reset));
endmodule

module ALU (
  input  [2:0] ALU_Operation,
  input  [31:0] In1,
  input  [31:0] In2,
  output Zero,
  output [31:0] Result
);

  wire comparator_1_lt;
  wire [31:0] adder_1_out, and_1_out, bit_extender_1_out, nor_1_out, or_1_out, subtractor_1_out;

  assign and_1_out = In1 & In2;  // AND_Gate and_1, 32 bits wide
  assign or_1_out = In1 | In2;  // OR_Gate or_1, 32 bits wide
  Adder #(.width(32)) adder_1 (.a(In1), .b(In2), .out(adder_1_out));  // open: cin, cout
  Subtractor #(.width(32)) subtractor_1 (.a(In1), .b(In2), .out(subtractor_1_out));  // open: bin, bout
  assign bit_extender_1_out = {{31{1'b0}}, comparator_1_lt};  // Bit_Extender bit_extender_1
  Comparator #(.width(32)) comparator_1 (.a(In1), .b(In2), .lt(comparator_1_lt));  // open: gt, eq
  assign nor_1_out = ~(In1 | In2);  // NOR_Gate nor_1, 32 bits wide
  Multiplexer #(.select(3), .width(32)) multiplexer_1 (
    .in0(and_1_out), .in1(or_1_out), .in2(adder_1_out), .in3(subtractor_1_out), .in4(bit_extender_1_out),
    .in5(nor_1_out), .in6({32{1'b0}}), .out(Result), .sel(ALU_Operation));  // open: in7
  Comparator #(.width(32)) comparator_2 (.a({32{1'b0}}), .b(Result), .eq(Zero));  // open: gt, lt
endmodule

module ALU_control (
  input  [1:0] ALUOp,
  input  [5:0] funct,
  output [2:0] ALU_Operation,
  output jr
);

  wire and_1_out, and_2_out, and_3_out, and_4_out, and_5_out, not_1_out, not_2_out, not_3_out, not_4_out,
       not_5_out, not_6_out, not_7_out, not_8_out;

  not not_1 (not_1_out, ALUOp[1]);
  not not_2 (not_2_out, ALUOp[0]);
  not not_3 (not_3_out, funct[5]);
  not not_4 (not_4_out, funct[4]);
  not not_5 (not_5_out, funct[3]);
  not not_6 (not_6_out, funct[2]);
  not not_7 (not_7_out, funct[1]);
  not not_8 (not_8_out, funct[0]);
  and and_1 (and_1_out, ALUOp[1], funct[2], funct[1]);
  and and_2 (and_2_out, ALUOp[1], funct[3]);
  and and_3 (and_3_out, not_5_out, not_6_out);
  and and_4 (and_4_out, ALUOp[1], funct[0]);
  and and_5 (and_5_out, ALUOp[1], not_5_out, funct[1]);
  and and_6 (jr, ALUOp[1], not_2_out, not_3_out, not_4_out, funct[3], not_6_out, not_7_out, not_8_out);
  or or_1 (ALU_Operation[2], and_1_out, and_2_out);
  or or_2 (ALU_Operation[1], not_1_out, not_3_out, and_3_out);
  or or_3 (ALU_Operation[0], ALUOp[0], and_4_out, and_5_out);
endmodule

module Control (
  input  [5:0] Opcode,
  output RegDst,
  output ALUSrc,
  output MemtoReg,
  output RegWrite,
  output MemRead,
  output MemWrite,
  output BranchEqual,
  output BranchNotEqual,
  output [1:0] ALUOp,
  output Jump,
  output Link,
  output lbu
);

  wire and_2_out, and_3_out, and_4_out, not_1_out, not_2_out, not_3_out, not_4_out, not_5_out;

  not not_1 (not_1_out, Opcode[5]);
  not not_2 (not_2_out, Opcode[3]);
  not not_3 (not_3_out, Opcode[2]);
  not not_4 (not_4_out, Opcode[1]);
  not not_5 (not_5_out, Opcode[0]);
  and and_1 (RegDst, not_1_out, not_2_out);
  or or_1 (ALUSrc, Opcode[3], Opcode[5]);
  or or_2 (MemtoReg, Opcode[0], Opcode[5]);
  and and_2 (and_2_out, not_3_out, not_4_out);
  and and_3 (and_3_out, not_2_out, not_3_out, Opcode[0]);
  and and_4 (and_4_out, Opcode[5], not_2_out);
  and and_5 (MemRead, Opcode[5], not_2_out);
  and and_6 (MemWrite, Opcode[5], Opcode[3]);
  and and_7 (BranchEqual, not_1_out, Opcode[2], not_5_out);
  and and_8 (BranchNotEqual, not_4_out, Opcode[0]);
  and and_9 (ALUOp[1], not_1_out, not_2_out, not_3_out);
  and and_10 (ALUOp[0], not_1_out, Opcode[2]);
  and and_11 (Jump, not_1_out, Opcode[1]);
  and and_12 (Link, not_1_out, not_3_out, Opcode[0]);
  and and_13 (lbu, Opcode[5], Opcode[2]);
  or or_3 (RegWrite, and_2_out, and_3_out, and_4_out);
endmodule

module Instruction_memory (
  input  [31:0] ReadAddress,
  output [31:0] Instruction
);

  ROM #(.addrWidth(24), .dataWidth(32)) rom_1 (.addr(ReadAddress[25:2]), .data(Instruction));

  // Notes on the sheet:
  //   contents of rom_1 (hex, n*v repeats v):
  //   2008005e ad280000 21290004 2008fffe ad280000 21290004 20080002 ad280000 21290004 2008ffd2 ad280000
  //   21290004 20080023 ad280000 21290004 2008000c ad280000 21290004 2008ffea ad280000 21290004 20080041
  //   ad280000 21290004 2008ffff ad280000 21290004 20080060 ad280000 21290004 2008005a ad280000 21290004
  //   2008ffd1 ad280000 21290004 20080052 ad280000 21290004 2008ffd2 ad280000 21290004 2008ffa4 ad280000
  //   21290004 2008004a ad280000 21290004 20080041 ad280000 21290004 2008ffde ad280000 21290004 20080036
  //   ad280000 21290004 20080005 ad280000 21290004 c000043 28820 39020 c000058 29820 3a020 800006d 6020
  //   20080000 8d090000 96820 21080008 8d0a0000 149582a 20010000 102b0001 a4820 14d582a 20010001 102b0001
  //   a6820 218c0001 20010013 102c0001 8000047 91020 d1820 3e00008 6020 20880004 8d090000 96820 21080008
  //   8d0a0000 149582a 20010000 102b0001 a4820 14d582a 20010001 102b0001 a6820 218c0001 20010013 102c0001
  //   800005c 91020 d1820 3e00008
endmodule

module Data_memory (
  input  [31:0] Address,
  input  MemWrite,
  input  MemRead,
  input  lbu,
  input  CLK,
  input  [31:0] WriteData,
  output [31:0] ReadData
);

  wire [7:0] multiplexer_1_out;
  wire [31:0] bit_extender_1_out, ram_1_dout;

  RAM #(.addrWidth(24), .asyncread("true"), .dataWidth(32)) ram_1 (
    .addr(Address[25:2]), .we(MemWrite), .oe(MemRead), .clk(CLK), .din(WriteData), .dout(ram_1_dout));
  Multiplexer #(.select(2), .width(8)) multiplexer_1 (
    .in0(ram_1_dout[7:0]), .in1(ram_1_dout[15:8]), .in2(ram_1_dout[23:16]), .in3(ram_1_dout[31:24]),
    .out(multiplexer_1_out), .sel(Address[1:0]));
  assign bit_extender_1_out = {{24{1'b0}}, multiplexer_1_out};  // Bit_Extender bit_extender_1
  Multiplexer #(.width(32)) multiplexer_2 (.in0(ram_1_dout), .in1(bit_extender_1_out), .out(ReadData), .sel(lbu));
endmodule
