// Logisim project monocicle-cpu.circ as structural Verilog: 8 circuits, main circuit main
module main (
);

  wire alu_1_zero, and_1_out, CLK, control_1_alusrc, control_1_branch, control_1_jump, control_1_lh,
       control_1_memread, control_1_memtoreg, control_1_memwrite, control_1_regdst, control_1_regwrite, jr,
       PCData, Reset;
  wire [1:0] control_1_aluop;
  wire [2:0] alu_control_1_aluctrl;
  wire [3:0] InstructionMemory_pc4;
  wire [4:0] lbdown_1_rd, lbdown_1_rs, lbdown_1_rt, multiplexer_1_out;
  wire [5:0] lbdown_1_funct, lbdown_1_op;
  wire [15:0] lbdown_1_imm;
  wire [25:0] lbdown_1_address;
  wire [27:0] bit_extender_1_out, InstructionMemory_pc4_2, shifter_1_out;
  wire [31:0] adder_1_out, alu_1_result, bit_extender_2_out, data_memory_1_readdata,
       InstructionMemory_instruction, multiplexer_2_out, multiplexer_3_out, multiplexer_4_out,
       multiplexer_5_out, multiplexer_6_out, multiplexer_7_out, Reg1, reg_file_1_read_data2, shifter_2_out;

  Clock u_CLK (.out(CLK));
  Button u_RESET (.out(Reset));
  Fetch InstructionMemory (
    .PC4({InstructionMemory_pc4, InstructionMemory_pc4_2}), .Instruction(InstructionMemory_instruction),
    .PCin(multiplexer_6_out), .CLK(CLK), .RESET(Reset));
  // Probe on InstructionMemory_instruction
  lbdown lbdown_1 (
    .op(lbdown_1_op), .rs(lbdown_1_rs), .rt(lbdown_1_rt), .rd(lbdown_1_rd), .funct(lbdown_1_funct),
    .Address(lbdown_1_address), .Imm(lbdown_1_imm), .Instruction(InstructionMemory_instruction));  // open: shamt
  assign bit_extender_1_out = {{2{1'b0}}, lbdown_1_address};  // Bit_Extender bit_extender_1
  Shifter #(.width(28)) shifter_1 (.in(bit_extender_1_out), .\dist (5'b00010), .out(shifter_1_out));
  Control control_1 (
    .RegDst(control_1_regdst), .ALUSrc(control_1_alusrc), .MemtoReg(control_1_memtoreg),
    .RegWrite(control_1_regwrite), .MemRead(control_1_memread), .MemWrite(control_1_memwrite),
    .Branch(control_1_branch), .ALUOp(control_1_aluop), .Jump(control_1_jump), .PCData(PCData),
    .lh(control_1_lh), .OpCode(lbdown_1_op));
  ALU_Control alu_control_1 (
    .ALUCtrl(alu_control_1_aluctrl), .jr(jr), .Funct(lbdown_1_funct), .OpCode(control_1_aluop));
  Multiplexer #(.width(5)) multiplexer_1 (
    .in0(lbdown_1_rt), .in1(lbdown_1_rd), .out(multiplexer_1_out), .sel(control_1_regdst));
  Multiplexer #(.width(32)) multiplexer_2 (
    .in0(multiplexer_7_out), .in1({InstructionMemory_pc4, InstructionMemory_pc4_2}), .out(multiplexer_2_out),
    .sel(PCData));
  assign bit_extender_2_out = {{16{lbdown_1_imm[15]}}, lbdown_1_imm};  // Bit_Extender bit_extender_2
  Reg_File reg_file_1 (
    .Read_Data1(Reg1), .Read_Data2(reg_file_1_read_data2), .Read_Reg1(lbdown_1_rs),
    .WriteEnable(control_1_regwrite), .CLK(CLK), .RESET(Reset), .Read_Reg2(lbdown_1_rt),
    .WriteReg(multiplexer_1_out), .WriteData(multiplexer_2_out));
  Shifter #(.width(32)) shifter_2 (.in(bit_extender_2_out), .\dist (5'b00010), .out(shifter_2_out));
  Multiplexer #(.width(32)) multiplexer_3 (
    .in0(reg_file_1_read_data2), .in1(bit_extender_2_out), .out(multiplexer_3_out), .sel(control_1_alusrc));
  Adder #(.width(32)) adder_1 (
    .a({InstructionMemory_pc4, InstructionMemory_pc4_2}), .b(shifter_2_out), .out(adder_1_out));  // open: cin, cout
  ALU alu_1 (
    .ZERO(alu_1_zero), .Result(alu_1_result), .In1(Reg1), .In2(multiplexer_3_out),
    .ALU_Operation(alu_control_1_aluctrl));
  Multiplexer #(.width(32)) multiplexer_4 (
    .in0({InstructionMemory_pc4, InstructionMemory_pc4_2}), .in1(adder_1_out), .out(multiplexer_4_out),
    .sel(and_1_out));
  and and_1 (and_1_out, control_1_branch, alu_1_zero);
  Multiplexer #(.width(32)) multiplexer_5 (
    .in0(multiplexer_4_out), .in1({InstructionMemory_pc4, shifter_1_out}), .out(multiplexer_5_out),
    .sel(control_1_jump));
  Multiplexer #(.width(32)) multiplexer_6 (.in0(multiplexer_5_out), .in1(Reg1), .out(multiplexer_6_out), .sel(jr));
  Data_Memory data_memory_1 (
    .ReadData(data_memory_1_readdata), .lh(control_1_lh), .Address(alu_1_result),
    .WriteData(reg_file_1_read_data2), .MemWrite(control_1_memwrite), .MemRead(control_1_memread), .CLK(CLK));
  Multiplexer #(.width(32)) multiplexer_7 (
    .in0(alu_1_result), .in1(data_memory_1_readdata), .out(multiplexer_7_out), .sel(control_1_memtoreg));

  // Notes on the sheet:
  //   jal
  //   beq
  //   Jump
  //   Jump Reg
endmodule

module Fetch (
  input  [31:0] PCin,
  input  CLK,
  input  RESET,
  output [31:0] PC4,
  output [31:0] Instruction
);

  wire [31:0] PC_q;

  Register #(.width(32)) PC (.D(PCin), .en(1'b1), .clk(CLK), .Q(PC_q), .clr(RESET));
  // Probe on PC_q
  Adder #(.width(32)) adder_1 (.a(PC_q), .b(32'h4), .out(PC4));  // open: cin, cout
  // Probe on PC_q[25:2]
  ROM #(.addrWidth(24), .dataWidth(32)) InstructionMemory (.addr(PC_q[25:2]), .data(Instruction));

  // Notes on the sheet:
  //   contents of InstructionMemory (hex, n*v repeats v):
  //   2020 8c050064 20100001 20110001 8c920000 121020 121820 205402a 11000008 20840004 8c920000 242402a
  //   11000029 72402a 11000029 22100001 8000007 acc20068 acc30090 20c60004 22310001 20100000 8c820004
  //   8c830004 b1402a 1100ffed 2020 20070004 20100001 20110001 8c920000 121020 121820 205402a 11000008
  //   20840014 8c920000 242402a 11000013 72402a 11000013 22100001 8000021 acc20068 acc30090 20c60004
  //   22310001 20100001 8ce20000 8ce30000 72020 20e70004 b1402a 1100ffeb 121020 800000f 121820 800000f
  //   121020 8000029 121820 8000029
endmodule

module lbdown (
  input  [31:0] Instruction,
  output [5:0] funct,
  output [4:0] shamt,
  output [4:0] rd,
  output [4:0] rt,
  output [15:0] Imm,
  output [4:0] rs,
  output [5:0] op,
  output [25:0] Address
);


  assign Address = Instruction[25:0];
  assign funct = Instruction[5:0];
  assign Imm = Instruction[15:0];
  assign op = Instruction[31:26];
  assign rd = Instruction[15:11];
  assign rs = Instruction[25:21];
  assign rt = Instruction[20:16];
  assign shamt = Instruction[10:6];
endmodule

module Reg_File (
  input  [31:0] WriteData,
  input  WriteEnable,
  input  [4:0] WriteReg,
  input  [4:0] Read_Reg1,
  input  [4:0] Read_Reg2,
  input  CLK,
  input  RESET,
  output [31:0] Read_Data1,
  output [31:0] Read_Data2
);

  wire decoder_1_out0, decoder_1_out1, decoder_1_out2, decoder_1_out3, decoder_1_out4, decoder_1_out5,
       decoder_1_out6, decoder_1_out7, decoder_1_out8, decoder_1_out9, decoder_1_out10, decoder_1_out11,
       decoder_1_out12, decoder_1_out13, decoder_1_out14, decoder_1_out15, decoder_1_out16, decoder_1_out17,
       decoder_1_out18, decoder_1_out19, decoder_1_out20, decoder_1_out21, decoder_1_out22, decoder_1_out23,
       decoder_1_out24, decoder_1_out25, decoder_1_out26, decoder_1_out27, decoder_1_out28, decoder_1_out29,
       decoder_1_out30, decoder_1_out31;
  wire [31:0] R1, R2, R3, R4, R5, R6, R7, R8, R9, R10, R11, R12, R13, R14, R15, R16, R17, R18, R19, R20, R21,
       R22, R23, R24, R25, R26, R27, R28, R29, R30, R31, Zero;

  Decoder #(.select(5)) decoder_1 (
    .out0(decoder_1_out0), .out1(decoder_1_out1), .out2(decoder_1_out2), .out3(decoder_1_out3),
    .out4(decoder_1_out4), .out5(decoder_1_out5), .out6(decoder_1_out6), .out7(decoder_1_out7),
    .out8(decoder_1_out8), .out9(decoder_1_out9), .out10(decoder_1_out10), .out11(decoder_1_out11),
    .out12(decoder_1_out12), .out13(decoder_1_out13), .out14(decoder_1_out14), .out15(decoder_1_out15),
    .out16(decoder_1_out16), .out17(decoder_1_out17), .out18(decoder_1_out18), .out19(decoder_1_out19),
    .out20(decoder_1_out20), .out21(decoder_1_out21), .out22(decoder_1_out22), .out23(decoder_1_out23),
    .out24(decoder_1_out24), .out25(decoder_1_out25), .out26(decoder_1_out26), .out27(decoder_1_out27),
    .out28(decoder_1_out28), .out29(decoder_1_out29), .out30(decoder_1_out30), .out31(decoder_1_out31),
    .sel(WriteReg), .en(WriteEnable));
  Register #(.width(32)) u_ZERO (.D({32{1'b0}}), .en(decoder_1_out0), .clk(CLK), .Q(Zero), .clr(RESET));
  Register #(.width(32)) register_1 (.D(WriteData), .en(decoder_1_out4), .clk(CLK), .Q(R4), .clr(RESET));
  Register #(.width(32)) register_2 (.D(WriteData), .en(decoder_1_out8), .clk(CLK), .Q(R8), .clr(RESET));
  Register #(.width(32)) register_3 (.D(WriteData), .en(decoder_1_out12), .clk(CLK), .Q(R12), .clr(RESET));
  Register #(.width(32)) register_4 (.D(WriteData), .en(decoder_1_out16), .clk(CLK), .Q(R16), .clr(RESET));
  Register #(.width(32)) register_5 (.D(WriteData), .en(decoder_1_out20), .clk(CLK), .Q(R20), .clr(RESET));
  Register #(.width(32)) register_6 (.D(WriteData), .en(decoder_1_out24), .clk(CLK), .Q(R24), .clr(RESET));
  Register #(.width(32)) register_7 (.D(WriteData), .en(decoder_1_out28), .clk(CLK), .Q(R28), .clr(RESET));
  Register #(.width(32)) register_8 (.D(WriteData), .en(decoder_1_out1), .clk(CLK), .Q(R1), .clr(RESET));
  Register #(.width(32)) register_9 (.D(WriteData), .en(decoder_1_out5), .clk(CLK), .Q(R5), .clr(RESET));
  Register #(.width(32)) register_10 (.D(WriteData), .en(decoder_1_out9), .clk(CLK), .Q(R9), .clr(RESET));
  Register #(.width(32)) register_11 (.D(WriteData), .en(decoder_1_out13), .clk(CLK), .Q(R13), .clr(RESET));
  Register #(.width(32)) register_12 (.D(WriteData), .en(decoder_1_out17), .clk(CLK), .Q(R17), .clr(RESET));
  Register #(.width(32)) register_13 (.D(WriteData), .en(decoder_1_out21), .clk(CLK), .Q(R21), .clr(RESET));
  Register #(.width(32)) register_14 (.D(WriteData), .en(decoder_1_out25), .clk(CLK), .Q(R25), .clr(RESET));
  Register #(.width(32)) register_15 (.D(WriteData), .en(decoder_1_out29), .clk(CLK), .Q(R29), .clr(RESET));
  Register #(.width(32)) register_16 (.D(WriteData), .en(decoder_1_out2), .clk(CLK), .Q(R2), .clr(RESET));
  Register #(.width(32)) register_17 (.D(WriteData), .en(decoder_1_out6), .clk(CLK), .Q(R6), .clr(RESET));
  Register #(.width(32)) register_18 (.D(WriteData), .en(decoder_1_out10), .clk(CLK), .Q(R10), .clr(RESET));
  Register #(.width(32)) register_19 (.D(WriteData), .en(decoder_1_out14), .clk(CLK), .Q(R14), .clr(RESET));
  Register #(.width(32)) register_20 (.D(WriteData), .en(decoder_1_out18), .clk(CLK), .Q(R18), .clr(RESET));
  Register #(.width(32)) register_21 (.D(WriteData), .en(decoder_1_out22), .clk(CLK), .Q(R22), .clr(RESET));
  Register #(.width(32)) register_22 (.D(WriteData), .en(decoder_1_out26), .clk(CLK), .Q(R26), .clr(RESET));
  Register #(.width(32)) register_23 (.D(WriteData), .en(decoder_1_out30), .clk(CLK), .Q(R30), .clr(RESET));
  Register #(.width(32)) register_24 (.D(WriteData), .en(decoder_1_out3), .clk(CLK), .Q(R3), .clr(RESET));
  Register #(.width(32)) register_25 (.D(WriteData), .en(decoder_1_out7), .clk(CLK), .Q(R7), .clr(RESET));
  Register #(.width(32)) register_26 (.D(WriteData), .en(decoder_1_out11), .clk(CLK), .Q(R11), .clr(RESET));
  Register #(.width(32)) register_27 (.D(WriteData), .en(decoder_1_out15), .clk(CLK), .Q(R15), .clr(RESET));
  Register #(.width(32)) register_28 (.D(WriteData), .en(decoder_1_out19), .clk(CLK), .Q(R19), .clr(RESET));
  Register #(.width(32)) register_29 (.D(WriteData), .en(decoder_1_out23), .clk(CLK), .Q(R23), .clr(RESET));
  Register #(.width(32)) register_30 (.D(WriteData), .en(decoder_1_out27), .clk(CLK), .Q(R27), .clr(RESET));
  Register #(.width(32)) register_31 (.D(WriteData), .en(decoder_1_out31), .clk(CLK), .Q(R31), .clr(RESET));
  Multiplexer #(.select(5), .width(32)) multiplexer_1 (
    .in0(Zero), .in1(R1), .in2(R2), .in3(R3), .in4(R4), .in5(R5), .in6(R6), .in7(R7), .in8(R8), .in9(R9),
    .in10(R10), .in11(R11), .in12(R12), .in13(R13), .in14(R14), .in15(R15), .in16(R16), .in17(R17),
    .in18(R18), .in19(R19), .in20(R20), .in21(R21), .in22(R22), .in23(R23), .in24(R24), .in25(R25),
    .in26(R26), .in27(R27), .in28(R28), .in29(R29), .in30(R30), .in31(R31), .out(Read_Data1), .sel(Read_Reg1));
  Multiplexer #(.select(5), .width(32)) multiplexer_2 (
    .in0(Zero), .in1(R1), .in2(R2), .in3(R3), .in4(R4), .in5(R5), .in6(R6), .in7(R7), .in8(R8), .in9(R9),
    .in10(R10), .in11(R11), .in12(R12), .in13(R13), .in14(R14), .in15(R15), .in16(R16), .in17(R17),
    .in18(R18), .in19(R19), .in20(R20), .in21(R21), .in22(R22), .in23(R23), .in24(R24), .in25(R25),
    .in26(R26), .in27(R27), .in28(R28), .in29(R29), .in30(R30), .in31(R31), .out(Read_Data2), .sel(Read_Reg2));
endmodule

module ALU (
  input  [31:0] In1,
  input  [31:0] In2,
  input  [2:0] ALU_Operation,
  output ZERO,
  output [31:0] Result
);

  wire [0:0] SLT;
  wire [31:0] Add, LAnd, LNor, LOr, Sub;

  Comparator #(.width(32)) comparator_1 (.a(In1), .b(In2), .lt(SLT[0]));  // open: gt, eq
  Multiplexer #(.select(3), .width(32)) multiplexer_1 (
    .in0(LAnd), .in1(LOr), .in2(Add), .in3(Sub), .in4({{31{1'b0}}, SLT[0]}), .in5(LNor), .in6({32{1'b0}}),
    .out(Result), .sel(ALU_Operation));  // open: in7
  Comparator #(.width(32)) comparator_2 (.a({32{1'b0}}), .b(Result), .eq(ZERO));  // open: gt, lt
  Adder #(.width(32)) adder_1 (.a(In1), .b(In2), .out(Add));  // open: cin, cout
  Subtractor #(.width(32)) subtractor_1 (.a(In1), .b(In2), .out(Sub));  // open: bin, bout
  assign LAnd = In1 & In2;  // AND_Gate and_1, 32 bits wide
  assign LOr = In1 | In2;  // OR_Gate or_1, 32 bits wide
  assign LNor = ~(In1 | In2);  // NOR_Gate nor_1, 32 bits wide

  // Other names for the same wires on the sheet: Num_1[31:0] = In1; Num_2[31:0] = In2
endmodule

module Control (
  input  [5:0] OpCode,
  output RegDst,
  output ALUSrc,
  output MemtoReg,
  output RegWrite,
  output MemRead,
  output MemWrite,
  output Branch,
  output [1:0] ALUOp,
  output Jump,
  output PCData,
  output lh
);

  wire and_2_out, and_3_out, not_1_out, not_2_out, not_3_out, not_4_out, not_5_out, not_6_out;

  not not_1 (not_1_out, OpCode[5]);
  not not_2 (not_2_out, OpCode[4]);
  not not_3 (not_3_out, OpCode[3]);
  not not_4 (not_4_out, OpCode[2]);
  not not_5 (not_5_out, OpCode[1]);
  not not_6 (not_6_out, OpCode[0]);
  and and_1 (RegDst, not_1_out, not_3_out);
  or or_1 (ALUSrc, OpCode[3], OpCode[5]);
  and and_2 (and_2_out, not_4_out, not_5_out);
  and and_3 (and_3_out, not_3_out, OpCode[0]);
  and and_4 (MemRead, OpCode[5], not_3_out);
  and and_5 (MemWrite, OpCode[3], OpCode[1]);
  and and_6 (ALUOp[1], not_3_out, not_4_out, not_6_out);
  and and_7 (Jump, not_1_out, OpCode[1]);
  and and_8 (PCData, not_1_out, OpCode[1]);
  and and_9 (lh, OpCode[5], not_2_out, not_3_out, not_4_out, not_5_out, OpCode[0]);
  or or_2 (RegWrite, and_2_out, and_3_out);

  assign ALUOp[0] = OpCode[2];
  assign Branch = OpCode[2];
  assign MemtoReg = OpCode[5];
endmodule

module ALU_Control (
  input  [5:0] Funct,
  input  [1:0] OpCode,
  output [2:0] ALUCtrl,
  output jr
);

  wire and_1_out, and_2_out, and_3_out, and_4_out, and_5_out, and_6_out, not_1_out, not_2_out, not_3_out,
       not_4_out, not_5_out, not_6_out, not_7_out, not_8_out;

  not not_1 (not_1_out, OpCode[1]);
  not not_2 (not_2_out, OpCode[0]);
  not not_3 (not_3_out, Funct[5]);
  not not_4 (not_4_out, Funct[4]);
  not not_5 (not_5_out, Funct[3]);
  not not_6 (not_6_out, Funct[2]);
  not not_7 (not_7_out, Funct[1]);
  not not_8 (not_8_out, Funct[0]);
  and and_1 (and_1_out, OpCode[1], Funct[2], Funct[1]);
  or or_1 (ALUCtrl[2], and_1_out, and_2_out);
  and and_2 (and_2_out, OpCode[1], Funct[3]);
  or or_2 (ALUCtrl[1], not_1_out, and_3_out);
  and and_3 (and_3_out, not_5_out, not_6_out);
  and and_4 (and_4_out, not_1_out, OpCode[0]);
  and and_5 (and_5_out, OpCode[1], not_2_out, not_4_out, not_5_out, not_6_out, Funct[1], not_8_out);
  or or_3 (ALUCtrl[0], and_4_out, and_5_out, and_6_out);
  and and_6 (and_6_out, OpCode[1], not_2_out, Funct[5], not_4_out, not_5_out, Funct[2], Funct[0]);
  and and_7 (jr, OpCode[1], not_2_out, not_3_out, not_4_out, Funct[3], not_6_out, not_7_out, not_8_out);
endmodule

module Data_Memory (
  input  MemWrite,
  input  MemRead,
  input  CLK,
  input  [31:0] WriteData,
  input  lh,
  input  [31:0] Address,
  output [31:0] ReadData
);

  wire Sel;
  wire [1:1] divider_1_out;
  wire [15:0] multiplexer_1_out;
  wire [31:0] bit_extender_1_out, ram_1_dout;

  // Probe on Address[1:0]
  // Probe on Sel
  Divider #(.width(2)) divider_1 (.a(Address[1:0]), .b(2'b10), .out({divider_1_out[1], Sel}));  // open: upper, rem
  // Probe on Address[25:2]
  RAM #(.addrWidth(24), .asyncread("true"), .dataWidth(32)) ram_1 (
    .addr(Address[25:2]), .we(MemWrite), .oe(MemRead), .clk(CLK), .din(WriteData), .dout(ram_1_dout));
  // Probe on ram_1_dout[15:0]
  Multiplexer #(.width(16)) multiplexer_1 (
    .in0(ram_1_dout[15:0]), .in1(ram_1_dout[31:16]), .out(multiplexer_1_out), .sel(Sel));
  assign bit_extender_1_out = {{16{multiplexer_1_out[15]}}, multiplexer_1_out};  // Bit_Extender bit_extender_1
  Multiplexer #(.width(32)) multiplexer_2 (.in0(ram_1_dout), .in1(bit_extender_1_out), .out(ReadData), .sel(lh));

  // Notes on the sheet:
  //   load halfword
endmodule
